// Logisim project brainFComputer.circ as structural Verilog: 1 circuit, main circuit main
module main (
);

  wire and_1_out, clock, clock_1_out, codeMovement, comparator_1_eq, comparator_2_eq, comparator_3_eq,
       comparator_4_eq, comparator_5_eq, comparator_6_eq, comparator_7_eq, comparator_9_eq, keyboard_1_avail,
       nor_1_out, not_1_out, not_2_out, not_3_out, not_4_out, or_1_out, or_2_out, or_4_out, pauseClock,
       screenActivation;
  wire [3:0] ram_1_data;
  wire [6:0] keyboard_1_data, register_5_q;
  wire [15:0] adder_1_out, controlled_buffer_1_out, ram_1_data_2, register_2_q;
  wire [23:0] adder_2_out, controlled_buffer_3_out, register_3_q, subtractor_1_out;
  wire [24:0] register_5_q_2;
  wire [31:0] adder_3_out, bit_extender_1_out, controlled_buffer_6_out, controlled_buffer_7_out,
       register_4_q, subtractor_2_out;

  Clock clock_1 (.out(clock_1_out));
  Register #(.width(1), .trigger("high")) register_1 (.D(clock_1_out), .Q(clock), .clk(not_1_out));  // open: en, clr
  not not_1 (not_1_out, pauseClock);
  not not_2 (not_2_out, or_1_out);
  assign controlled_buffer_1_out = or_1_out ? ram_1_data_2 : 16'bz;  // Controlled_Buffer controlled_buffer_1
  assign controlled_buffer_1_out = not_2_out ? adder_1_out : 16'bz;  // Controlled_Buffer controlled_buffer_2
  Register #(.width(16)) register_2 (
    .D(controlled_buffer_1_out), .en(1'b1), .Q(register_2_q), .clk(clock));  // open: clr
  nor nor_1 (nor_1_out, comparator_3_eq, comparator_1_eq);
  assign controlled_buffer_3_out = nor_1_out ? register_3_q : 24'bz;  // Controlled_Buffer controlled_buffer_3
  or or_1 (or_1_out, comparator_4_eq, and_1_out);
  Adder #(.width(16)) adder_1 (.a(register_2_q), .b(16'h1), .out(adder_1_out));  // open: cin, cout
  Comparator #(.width(4)) comparator_1 (.a(ram_1_data), .b(4'b0010), .eq(comparator_1_eq));  // open: gt, lt
  assign controlled_buffer_3_out = comparator_1_eq ? adder_2_out : 24'bz;  // Controlled_Buffer controlled_buffer_4
  and and_1 (and_1_out, comparator_5_eq, comparator_2_eq);
  Comparator #(.width(32)) comparator_2 (
    .a({32{1'b0}}), .b({register_5_q_2, register_5_q}), .eq(comparator_2_eq));  // open: gt, lt
  Comparator #(.width(4)) comparator_3 (.a(ram_1_data), .b(4'b0011), .eq(comparator_3_eq));  // open: gt, lt
  Adder #(.width(24)) adder_2 (.a(register_3_q), .b(24'h1), .out(adder_2_out));  // open: cin, cout
  assign controlled_buffer_3_out = comparator_3_eq ? subtractor_1_out : 24'bz;  // Controlled_Buffer controlled_buffer_5
  or or_2 (or_2_out, comparator_1_eq, comparator_3_eq);
  RAM #(.addrWidth(16), .dataWidth(20)) ram_1 (
    .addr(register_2_q), .data({ram_1_data_2, ram_1_data}), .clk(clock), .ld(1'b1));  // open: sel, clr
  Subtractor #(.width(24)) subtractor_1 (.a(register_3_q), .b(24'h1), .out(subtractor_1_out));  // open: bin, bout
  Register #(.width(24)) register_3 (
    .D(controlled_buffer_3_out), .en(or_2_out), .Q(register_3_q), .clk(clock));  // open: clr
  Comparator #(.width(4)) comparator_4 (.a(4'b0001), .b(ram_1_data), .eq(comparator_4_eq));  // open: gt, lt
  Comparator #(.width(4)) comparator_5 (.a(4'b0000), .b(ram_1_data), .eq(comparator_5_eq));  // open: gt, lt
  or or_3 (codeMovement, comparator_4_eq, comparator_5_eq);
  Comparator #(.width(4)) comparator_6 (.a(4'b0100), .b(ram_1_data), .eq(comparator_6_eq));  // open: gt, lt
  or or_4 (or_4_out, codeMovement, screenActivation, or_2_out);
  assign controlled_buffer_6_out = or_4_out ? {register_5_q_2, register_5_q} : 32'bz;  // Controlled_Buffer controlled_buffer_6
  Adder #(.width(32)) adder_3 (.a({register_5_q_2, register_5_q}), .b(32'h1), .out(adder_3_out));  // open: cin, cout
  assign controlled_buffer_7_out = not_3_out ? register_4_q : 32'bz;  // Controlled_Buffer controlled_buffer_7
  RAM #(.addrWidth(24), .dataWidth(32), .bus("asynch")) ram_2 (
    .addr(register_3_q), .data(controlled_buffer_7_out), .ld(clock));  // open: sel, clr
  assign controlled_buffer_6_out = comparator_6_eq ? adder_3_out : 32'bz;  // Controlled_Buffer controlled_buffer_8
  Register #(.width(32), .trigger("low")) register_4 (
    .D(controlled_buffer_6_out), .Q(register_4_q), .clk(clock));  // open: en, clr
  not not_3 (not_3_out, clock);
  Comparator #(.width(4)) comparator_7 (.a(4'b0101), .b(ram_1_data), .eq(comparator_7_eq));  // open: gt, lt
  Register #(.width(32), .trigger("falling")) register_5 (
    .D(controlled_buffer_7_out), .Q({register_5_q_2, register_5_q}), .clk(clock));  // open: en, clr
  Subtractor #(.width(32)) subtractor_2 (
    .a({register_5_q_2, register_5_q}), .b(32'h1), .out(subtractor_2_out));  // open: bin, bout
  assign controlled_buffer_6_out = comparator_7_eq ? subtractor_2_out : 32'bz;  // Controlled_Buffer controlled_buffer_9
  // Probe on register_5_q
  Comparator #(.width(4)) comparator_8 (.a(ram_1_data), .b(4'b0110), .eq(screenActivation));  // open: gt, lt
  Comparator #(.width(4)) comparator_9 (.a(4'b0111), .b(ram_1_data), .eq(comparator_9_eq));  // open: gt, lt
  TTY tty_1 (.data(register_5_q), .clk(clock), .we(screenActivation));  // open: clr
  Keyboard keyboard_1 (
    .clk(clock), .re(comparator_9_eq), .avail(keyboard_1_avail), .data(keyboard_1_data));  // open: clr
  not not_4 (not_4_out, keyboard_1_avail);
  and and_2 (pauseClock, not_4_out, comparator_9_eq);
  assign bit_extender_1_out = {{25{1'b0}}, keyboard_1_data};  // Bit_Extender bit_extender_1
  assign controlled_buffer_6_out = comparator_9_eq ? bit_extender_1_out : 32'bz;  // Controlled_Buffer controlled_buffer_10
endmodule
